# Fritzing sketch ampel (saved by Fritzing 0.8.7b)
breadboards: 1

parts:
  U1 = attiny85 [package=dip]
  J1 = female pin header, 4 pins [form="♀ (female)"]
  J2 = female pin header, 4 pins [form="♀ (female)"]
  R1 = Resistor [tolerance=±5% resistance=220 package=THT]
  R2 = Resistor [tolerance=±5% resistance=220 package=THT]
  R3 = Resistor [tolerance=±5% resistance=220 package=THT]
  VCC1 = 4 x AAA Battery Mount
  Fuse1 = Fuse with Handler [part_number=Htc-15m]
  R4 = Resistor [tolerance=±5% resistance=220 package=THT]
  R5 = Resistor [tolerance=±5% resistance=220 package=THT]
  R6 = Resistor [tolerance=±5% resistance=220 package=THT]
  S1 = Momentary Switch [package=ksa_sealed_tac_switch]  # not connected
  S2 = Pushbutton [package="[THT]"]  # not connected
  IC2 = DIP - 14 pins [chip_label=IC package="DIP (Dual Inline) [THT]"]  # not connected

nets:
  N1: U1.Pin_1, R6.Pin_0
  N2: U1.Pin_2, R5.Pin_0
  N3: U1.Pin_3, R4.Pin_0
  GND: U1.Pin_4, VCC1.-
  N4: U1.Pin_5, R3.Pin_0
  N5: U1.Pin_6, R2.Pin_0
  N6: U1.Pin_7, R1.Pin_0
  N7: U1.Pin_8, J1.pin1, J2.pin1, Fuse1.Connector2
  N8: J1.pin2, R1.Pin_1
  N9: J1.pin3, R2.Pin_1
  N10: J1.pin4, R3.Pin_1
  N11: J2.pin2, R4.Pin_1
  N12: J2.pin3, R5.Pin_1
  N13: J2.pin4, R6.Pin_1
  N14: VCC1.+, Fuse1.Connector1

custom parts:
  DIP - 14 pins: A DIP stand-in part for whatever IC you want. With 14 pins on a 300mil dual inline package (DIP) footprint.
